# Fritzing sketch Ir5 (saved by Fritzing 0.9.3b)
circuit board: 5.51409cm x 3.04684cm
breadboards: 1

parts:
  LED3 = LED - 5mm [color="Infrared (940nm)" package="5 mm [THT]"]
  LED4 = LED - 5mm [color="Infrared (940nm)" package="5 mm [THT]"]
  R2 = Resistor [tolerance=±5% resistance=10 package=THT]
  LED2 = LED - 5mm [color="Infrared (940nm)" package="5 mm [THT]"]
  R1 = Resistor [tolerance=±5% resistance=10 package=THT]
  LED1 = LED - 5mm [color="Infrared (940nm)" package="5 mm [THT]"]
  Q2 = Basic FET N-Channel [package="TO220 [THT]"]
  R3 = Resistor [tolerance=±5% resistance=100k package=THT]
  R4 = Resistor [tolerance=±5% resistance=100 package=THT]
  J2 = male pin header, 2 pins [form="♂ (male)"]
  J1 = male pin header, 4 pins [form="♂ (male)"]
  R5 = Resistor [tolerance=±5% resistance=10 package=THT]
  IrR1 = OSRB38C9AA
  LED5 = LED - 5mm [color="Red (633nm)" package="5 mm [THT]"]
  MCU1 = Raspberry Pi Zero
  Oled1 = OLED SSD1306

nets:
  N1: LED3.cathode, LED4.anode
  N2: LED3.anode, R2.Pin_1
  N3: LED4.cathode, LED1.cathode, Q2.drain
  N4: R2.Pin_0, R1.Pin_0, J2.pin1, MCU1.pin_2, MCU1.pin_4
  N5: LED2.cathode, LED1.anode
  N6: LED2.anode, R1.Pin_1
  N7: Q2.gate, R3.Pin_0, R4.Pin_0, LED5.anode
  GND: Q2.source, R3.Pin_1, J2.pin2, J1.pin1, R5.Pin_1, IrR1.GND, MCU1.pin_6, MCU1.pin_9, MCU1.pin_30, MCU1.pin_34, Oled1.GND
  N8: R4.Pin_1, MCU1.pin_11
  VCC: J1.pin2, IrR1.VCC, MCU1.pin_1, Oled1.VCC
  N9: J1.pin3, MCU1.pin_5, Oled1.SCL
  N10: J1.pin4, MCU1.pin_3, Oled1.SDA
  N11: R5.Pin_0, LED5.cathode
  N12: IrR1.OUT, MCU1.pin_7

custom parts:
  OSRB38C9AA: 7..4*6..2*5..25mm Infrared Receiiver Modulle
  OLED SSD1306: OLED powered by a SSD1306 driver over I2C interface.
